# Fritzing sketch MonitorNevera (saved by Fritzing 0.9.3b)
circuit board: 8.46667cm x 5.64444cm
breadboards: 1

parts:
  WeMos_D1_Mini1 = WeMos D1 Mini
  DS1 = DS18B20 1-Wire Temperature Sensor [part_number=DS18B20]
  DS2 = DS18B20 1-Wire Temperature Sensor [part_number=DS18B20]
  R1 = Resistor [tolerance=±5% resistance=4.7k package="2010 [SMD]"]

nets:
  3.3V: WeMos_D1_Mini1.3V3, DS1.VDD, DS2.VDD, R1.Pin_0
  N1: WeMos_D1_Mini1.D2, DS1.DQ, DS2.DQ, R1.Pin_1
  GND: WeMos_D1_Mini1.G, DS1.GND, DS2.GND

custom parts:
  WeMos D1 Mini: The D1 mini is a mini wifi board based on ESP-8266EX.
